// Logisim project logisim_design.circ as structural Verilog: 14 circuits, main circuit main
module main (
  input  [3:0] Address,
  input  [7:0] Data,
  input  RUN,
  output [3:0] out_4,
  output [3:0] out_5
);

  wire and_1_out, and_2_out, C_S_cp, C_S_ea, C_S_ep, C_S_eu, C_S_halt, C_S_nce, C_S_nei, C_S_nla, C_S_nlb,
       C_S_nli, C_S_nlm, C_S_nlo, C_S_su, Clear_RAM_out, CLK_out, controlled_buffer_1_out, not_1_out,
       not_2_out, not_3_out, RESET_out, Write_to_RAM_out;
  wire [3:0] IR_to_controller, MAR_to_ram, multiplexer_1_out;
  wire [7:0] ACC_to_add_sub, B_Reg_to_add_sub, Output_Reg_to_binary_display;

  Button Write_to_RAM (.out(Write_to_RAM_out));
  Button Clear_RAM (.out(Clear_RAM_out));
  Multiplexer #(.width(4)) multiplexer_1 (
    .in0(Address), .in1(MAR_to_ram), .out(multiplexer_1_out), .sel(RUN));  // open: en
  not not_1 (not_1_out, RUN);
  not not_2 (not_2_out, C_S_nce);
  ProgramCounter PC (.Cp(C_S_cp), .nCLK(controlled_buffer_1_out), .Output_to_Bus(out_5), .Ep(C_S_ep), .CLR(RESET_out));
  MAR MAR (.CLK(controlled_buffer_1_out), .From_Bus(out_5), .To_RAM(MAR_to_ram), .nLm(C_S_nlm), .CLR(RESET_out));
  and and_1 (and_1_out, ~RUN, Write_to_RAM_out);  // AND_Gate
  and and_2 (and_2_out, ~RUN, Clear_RAM_out);  // AND_Gate
  InstructionRegister IR (
    .CLK(controlled_buffer_1_out), .CLR(RESET_out), .From_Bus({out_4, out_5}), .To_Bus(out_5), .nLi(C_S_nli),
    .To_Controller(IR_to_controller), .nEi(C_S_nei));
  ControllerSequencer C_S (
    .CLK(controlled_buffer_1_out), .I7(IR_to_controller[3]), ._16(IR_to_controller[2]),
    .I5(IR_to_controller[1]), .I4(IR_to_controller[0]), .Cp(C_S_cp), .Ep(C_S_ep), .nLm(C_S_nlm),
    .nCE(C_S_nce), .nLi(C_S_nli), .nEi(C_S_nei), .nLa(C_S_nla), .Ea(C_S_ea), .Su(C_S_su), .Eu(C_S_eu),
    .nLb(C_S_nlb), .nLo(C_S_nlo), .HALT(C_S_halt));
  RAM_part #(.addrWidth(4), .bus("separate")) ram_1 (
    .addr(multiplexer_1_out), .din(Data), .data({out_4, out_5}), .str(not_1_out), .clk(and_1_out),
    .ld(not_2_out), .clr(and_2_out));  // open: sel
  not not_3 (not_3_out, C_S_halt);
  Button RESET (.out(RESET_out));
  Clock CLK (.out(CLK_out));
  assign controlled_buffer_1_out = not_3_out ? CLK_out : 1'bz;  // Controlled_Buffer controlled_buffer_1
  Accumulator ACC (
    .To_Add_Sub(ACC_to_add_sub), .From_Bus({out_4, out_5}), .To_Bus({out_4, out_5}), .nLa(C_S_nla),
    .Ea(C_S_ea), .CLK(controlled_buffer_1_out), .CLR(RESET_out));
  B_Register B_Reg (
    .CLK(controlled_buffer_1_out), .From_Bus({out_4, out_5}), .To_Add_Sub(B_Reg_to_add_sub), .nLb(C_S_nlb),
    .in_2(RESET_out));
  Output_Register Output_Reg (
    .CLK(controlled_buffer_1_out), .From_Bus({out_4, out_5}),
    .To_Binary_Display(Output_Reg_to_binary_display), .nLo(C_S_nlo), .in_2(RESET_out));
  AdderSubtractor A_S (
    .From_B_register(B_Reg_to_add_sub), .To_Bus({out_4, out_5}), .From_Accumulator(ACC_to_add_sub),
    .Su(C_S_su), .Eu(C_S_eu));
  Hex_Digit_Display hex_digit_display_1 (.value(Output_Reg_to_binary_display[7:4]));  // open: dp
  Hex_Digit_Display hex_digit_display_2 (.value(Output_Reg_to_binary_display[3:0]));  // open: dp
endmodule

module ProgramCounter (
  input  Cp,
  input  nCLK,
  input  Ep,
  input  CLR,
  output [3:0] Output_to_Bus
);

  wire half_adder_1_sum, half_adder_2_carry, half_adder_2_sum, half_adder_3_carry, half_adder_3_sum,
       half_adder_4_carry, half_adder_4_sum, not_1_out;
  wire [3:0] d_ff_4_q;

  not not_1 (not_1_out, nCLK);
  half_adder half_adder_1 (.A(half_adder_2_carry), .Sum(half_adder_1_sum), .B(d_ff_4_q[3]));  // open: Carry
  D_Flip_Flop d_ff_1 (.clk(not_1_out), .D(half_adder_1_sum), .Q(d_ff_4_q[3]), .reset(CLR));  // open: Qn, preset, en
  half_adder half_adder_2 (.A(half_adder_3_carry), .Sum(half_adder_2_sum), .B(d_ff_4_q[2]), .Carry(half_adder_2_carry));
  D_Flip_Flop d_ff_2 (.clk(not_1_out), .D(half_adder_2_sum), .Q(d_ff_4_q[2]), .reset(CLR));  // open: Qn, preset, en
  half_adder half_adder_3 (.A(half_adder_4_carry), .Sum(half_adder_3_sum), .B(d_ff_4_q[1]), .Carry(half_adder_3_carry));
  D_Flip_Flop d_ff_3 (.clk(not_1_out), .D(half_adder_3_sum), .Q(d_ff_4_q[1]), .reset(CLR));  // open: Qn, preset, en
  half_adder half_adder_4 (.A(Cp), .Sum(half_adder_4_sum), .B(d_ff_4_q[0]), .Carry(half_adder_4_carry));
  D_Flip_Flop d_ff_4 (.clk(not_1_out), .D(half_adder_4_sum), .Q(d_ff_4_q[0]), .reset(CLR));  // open: Qn, preset, en
  assign Output_to_Bus = Ep ? d_ff_4_q : 4'bz;  // Controlled_Buffer controlled_buffer_1
endmodule

module MAR (
  input  CLK,
  input  CLR,
  input  [3:0] From_Bus,
  input  nLm,
  output [3:0] To_RAM
);

  wire not_1_out;
  wire [3:0] controlled_buffer_1_out;

  assign controlled_buffer_1_out = not_1_out ? From_Bus : 4'bz;  // Controlled_Buffer controlled_buffer_1
  not not_1 (not_1_out, nLm);
  D_Flip_Flop d_ff_1 (.clk(CLK), .D(controlled_buffer_1_out[3]), .Q(To_RAM[3]), .reset(CLR));  // open: Qn, preset, en
  D_Flip_Flop d_ff_2 (.clk(CLK), .D(controlled_buffer_1_out[2]), .Q(To_RAM[2]), .reset(CLR));  // open: Qn, preset, en
  D_Flip_Flop d_ff_3 (.clk(CLK), .D(controlled_buffer_1_out[1]), .Q(To_RAM[1]), .reset(CLR));  // open: Qn, preset, en
  D_Flip_Flop D0 (.clk(CLK), .D(controlled_buffer_1_out[0]), .Q(To_RAM[0]), .reset(CLR));  // open: Qn, preset, en
endmodule

module RAM (
  input  [3:0] Address,
  input  [7:0] Data,
  input  nCE,
  output [7:0] Bus
);

  wire not_1_out;

  not not_1 (not_1_out, nCE);
  RAM_part #(.addrWidth(4), .bus("separate")) ram_1 (
    .addr(Address), .din(Data), .data(Bus), .ld(not_1_out));  // open: str, sel, clk, clr
endmodule

module InstructionRegister (
  input  nEi,
  input  CLK,
  input  CLR,
  input  [7:0] From_Bus,
  input  nLi,
  output [3:0] To_Bus,
  output [3:0] To_Controller
);

  wire not_1_out, not_2_out;
  wire [3:0] D0_q;
  wire [7:0] controlled_buffer_1_out;

  D_Flip_Flop D7 (
    .clk(CLK), .D(controlled_buffer_1_out[7]), .Q(To_Controller[3]), .reset(CLR));  // open: Qn, preset, en
  D_Flip_Flop d_ff_1 (
    .clk(CLK), .D(controlled_buffer_1_out[6]), .Q(To_Controller[2]), .reset(CLR));  // open: Qn, preset, en
  assign controlled_buffer_1_out = not_1_out ? From_Bus : 8'bz;  // Controlled_Buffer controlled_buffer_1
  not not_1 (not_1_out, nLi);
  D_Flip_Flop d_ff_2 (
    .clk(CLK), .D(controlled_buffer_1_out[5]), .Q(To_Controller[1]), .reset(CLR));  // open: Qn, preset, en
  D_Flip_Flop d_ff_3 (
    .clk(CLK), .D(controlled_buffer_1_out[4]), .Q(To_Controller[0]), .reset(CLR));  // open: Qn, preset, en
  D_Flip_Flop d_ff_4 (.clk(CLK), .D(controlled_buffer_1_out[3]), .Q(D0_q[3]), .reset(CLR));  // open: Qn, preset, en
  assign To_Bus = not_2_out ? D0_q : 4'bz;  // Controlled_Buffer controlled_buffer_2
  not not_2 (not_2_out, nEi);
  D_Flip_Flop d_ff_5 (.clk(CLK), .D(controlled_buffer_1_out[2]), .Q(D0_q[2]), .reset(CLR));  // open: Qn, preset, en
  D_Flip_Flop d_ff_6 (.clk(CLK), .D(controlled_buffer_1_out[1]), .Q(D0_q[1]), .reset(CLR));  // open: Qn, preset, en
  D_Flip_Flop D0 (.clk(CLK), .D(controlled_buffer_1_out[0]), .Q(D0_q[0]), .reset(CLR));  // open: Qn, preset, en
endmodule

module ControllerSequencer (
  input  CLK,
  input  I5,
  input  _16,
  input  I4,
  input  I7,
  output Cp,
  output Ep,
  output nLm,
  output nCE,
  output nLi,
  output nEi,
  output nLa,
  output Ea,
  output Su,
  output Eu,
  output nLb,
  output nLo,
  output HALT
);

  wire and_1_out, and_2_out, and_3_out, and_4_out, and_5_out, and_6_out, and_7_out, and_8_out, and_9_out,
       and_10_out, and_11_out, and_12_out, and_15_out, and_16_out, and_17_out, and_18_out,
       instruction_decoder_1_add, instruction_decoder_1_lda, instruction_decoder_1_out,
       instruction_decoder_1_sub, ring_counter_1_t3, ring_counter_1_t4, ring_counter_1_t5, ring_counter_1_t6;

  Clock clock_1 ();  // open: out
  ring_counter ring_counter_1 (
    .CLK(CLK), .T1(Ep), .T2(Cp), .T3(ring_counter_1_t3), .T4(ring_counter_1_t4), .T5(ring_counter_1_t5),
    .T6(ring_counter_1_t6));
  instruction_decoder instruction_decoder_1 (
    .I7(I7), .I6(_16), .I5(I5), .I4(I4), .LDA(instruction_decoder_1_lda), .ADD(instruction_decoder_1_add),
    .SUB(instruction_decoder_1_sub), .OUT(instruction_decoder_1_out), .HLT(HALT));
  and and_1 (and_1_out, ring_counter_1_t4, instruction_decoder_1_lda);
  and and_2 (and_2_out, ring_counter_1_t4, instruction_decoder_1_add);
  nor nor_1 (nLm, and_1_out, and_2_out, and_3_out, Ep);
  and and_3 (and_3_out, ring_counter_1_t4, instruction_decoder_1_sub);
  and and_4 (and_4_out, ring_counter_1_t5, instruction_decoder_1_lda);
  Hex_Digit_Display hex_digit_display_1 (.value({Cp, Ep, nLm, nCE}));  // open: dp
  and and_5 (and_5_out, instruction_decoder_1_sub, ring_counter_1_t5);
  and and_6 (and_6_out, instruction_decoder_1_add, ring_counter_1_t5);
  nor nor_2 (nCE, and_4_out, and_6_out, and_5_out, ring_counter_1_t3);
  and and_7 (and_7_out, ring_counter_1_t4, instruction_decoder_1_lda);
  not not_1 (nLi, ring_counter_1_t3);
  and and_8 (and_8_out, ring_counter_1_t4, instruction_decoder_1_add);
  and and_9 (and_9_out, ring_counter_1_t4, instruction_decoder_1_sub);
  nor nor_3 (nEi, and_7_out, and_8_out, and_9_out);
  and and_10 (and_10_out, ring_counter_1_t5, instruction_decoder_1_lda);
  and and_11 (and_11_out, instruction_decoder_1_add, ring_counter_1_t6);
  nor nor_4 (nLa, and_10_out, and_11_out, and_12_out);
  Hex_Digit_Display hex_digit_display_2 (.value({nLi, nEi, nLa, Ea}));  // open: dp
  and and_12 (and_12_out, instruction_decoder_1_sub, ring_counter_1_t6);
  and and_13 (Ea, ring_counter_1_t4, instruction_decoder_1_out);
  and and_14 (Su, ring_counter_1_t6, instruction_decoder_1_sub);
  and and_15 (and_15_out, ring_counter_1_t6, instruction_decoder_1_add);
  or or_1 (Eu, and_15_out, and_17_out);
  and and_16 (and_16_out, ring_counter_1_t5, instruction_decoder_1_add);
  and and_17 (and_17_out, ring_counter_1_t6, instruction_decoder_1_sub);
  nor nor_5 (nLb, and_16_out, and_18_out);
  and and_18 (and_18_out, ring_counter_1_t5, instruction_decoder_1_sub);
  nand nand_1 (nLo, instruction_decoder_1_out, ring_counter_1_t4);
  Hex_Digit_Display hex_digit_display_3 (.value({Su, Eu, nLb, nLo}));  // open: dp
endmodule

module Accumulator (
  input  Ea,
  input  CLK,
  input  CLR,
  input  [7:0] From_Bus,
  input  nLa,
  output [7:0] To_Add_Sub,
  output [7:0] To_Bus
);

  wire not_1_out;
  wire [7:0] controlled_buffer_1_out;

  D_Flip_Flop D7 (.clk(CLK), .D(controlled_buffer_1_out[7]), .Q(To_Add_Sub[7]), .reset(CLR));  // open: Qn, preset, en
  D_Flip_Flop d_ff_1 (
    .clk(CLK), .D(controlled_buffer_1_out[6]), .Q(To_Add_Sub[6]), .reset(CLR));  // open: Qn, preset, en
  assign controlled_buffer_1_out = not_1_out ? From_Bus : 8'bz;  // Controlled_Buffer controlled_buffer_1
  not not_1 (not_1_out, nLa);
  D_Flip_Flop d_ff_2 (
    .clk(CLK), .D(controlled_buffer_1_out[5]), .Q(To_Add_Sub[5]), .reset(CLR));  // open: Qn, preset, en
  assign To_Bus = Ea ? To_Add_Sub : 8'bz;  // Controlled_Buffer controlled_buffer_2
  D_Flip_Flop d_ff_3 (
    .clk(CLK), .D(controlled_buffer_1_out[4]), .Q(To_Add_Sub[4]), .reset(CLR));  // open: Qn, preset, en
  D_Flip_Flop d_ff_4 (
    .clk(CLK), .D(controlled_buffer_1_out[3]), .Q(To_Add_Sub[3]), .reset(CLR));  // open: Qn, preset, en
  D_Flip_Flop d_ff_5 (
    .clk(CLK), .D(controlled_buffer_1_out[2]), .Q(To_Add_Sub[2]), .reset(CLR));  // open: Qn, preset, en
  D_Flip_Flop d_ff_6 (
    .clk(CLK), .D(controlled_buffer_1_out[1]), .Q(To_Add_Sub[1]), .reset(CLR));  // open: Qn, preset, en
  D_Flip_Flop D0 (.clk(CLK), .D(controlled_buffer_1_out[0]), .Q(To_Add_Sub[0]), .reset(CLR));  // open: Qn, preset, en
endmodule

module AdderSubtractor (
  input  [7:0] From_B_register,
  input  Su,
  input  Eu,
  input  [7:0] From_Accumulator,
  output [7:0] To_Bus
);

  wire full_adder_2_cout, full_adder_3_cout, full_adder_4_cout, full_adder_5_cout, full_adder_6_cout,
       full_adder_7_cout, full_adder_8_cout, xor_1_out, xor_2_out, xor_3_out, xor_4_out, xor_5_out,
       xor_6_out, xor_7_out, xor_8_out;
  wire [7:0] full_adder_8_sum;

  assign To_Bus = Eu ? full_adder_8_sum : 8'bz;  // Controlled_Buffer controlled_buffer_1
  xor xor_1 (xor_1_out, Su, From_B_register[7]);
  full_adder full_adder_1 (
    .A(From_Accumulator[7]), .B(xor_1_out), .Cin(full_adder_3_cout), .Sum(full_adder_8_sum[7]));  // open: Cout
  xor xor_2 (xor_2_out, Su, From_B_register[6]);
  full_adder full_adder_2 (
    .A(From_Accumulator[5]), .B(xor_3_out), .Cin(full_adder_4_cout), .Sum(full_adder_8_sum[5]),
    .Cout(full_adder_2_cout));
  full_adder full_adder_3 (
    .A(From_Accumulator[6]), .B(xor_2_out), .Cin(full_adder_2_cout), .Sum(full_adder_8_sum[6]),
    .Cout(full_adder_3_cout));
  xor xor_3 (xor_3_out, Su, From_B_register[5]);
  full_adder full_adder_4 (
    .A(From_Accumulator[4]), .B(xor_4_out), .Cin(full_adder_5_cout), .Sum(full_adder_8_sum[4]),
    .Cout(full_adder_4_cout));
  xor xor_4 (xor_4_out, Su, From_B_register[4]);
  xor xor_5 (xor_5_out, Su, From_B_register[3]);
  full_adder full_adder_5 (
    .A(From_Accumulator[3]), .B(xor_5_out), .Cin(full_adder_6_cout), .Sum(full_adder_8_sum[3]),
    .Cout(full_adder_5_cout));
  xor xor_6 (xor_6_out, Su, From_B_register[2]);
  full_adder full_adder_6 (
    .A(From_Accumulator[2]), .B(xor_6_out), .Cin(full_adder_7_cout), .Sum(full_adder_8_sum[2]),
    .Cout(full_adder_6_cout));
  xor xor_7 (xor_7_out, Su, From_B_register[1]);
  full_adder full_adder_7 (
    .A(From_Accumulator[1]), .B(xor_7_out), .Cin(full_adder_8_cout), .Sum(full_adder_8_sum[1]),
    .Cout(full_adder_7_cout));
  xor xor_8 (xor_8_out, Su, From_B_register[0]);
  full_adder full_adder_8 (
    .A(From_Accumulator[0]), .B(xor_8_out), .Cin(Su), .Sum(full_adder_8_sum[0]), .Cout(full_adder_8_cout));
endmodule

module B_Register (
  input  CLK,
  input  in_2,
  input  [7:0] From_Bus,
  input  nLb,
  output [7:0] To_Add_Sub
);

  wire not_1_out;
  wire [7:0] controlled_buffer_1_out;

  D_Flip_Flop D7 (.clk(CLK), .D(controlled_buffer_1_out[7]), .Q(To_Add_Sub[7]), .reset(in_2));  // open: Qn, preset, en
  D_Flip_Flop d_ff_1 (
    .clk(CLK), .D(controlled_buffer_1_out[6]), .Q(To_Add_Sub[6]), .reset(in_2));  // open: Qn, preset, en
  assign controlled_buffer_1_out = not_1_out ? From_Bus : 8'bz;  // Controlled_Buffer controlled_buffer_1
  not not_1 (not_1_out, nLb);
  D_Flip_Flop d_ff_2 (
    .clk(CLK), .D(controlled_buffer_1_out[5]), .Q(To_Add_Sub[5]), .reset(in_2));  // open: Qn, preset, en
  D_Flip_Flop d_ff_3 (
    .clk(CLK), .D(controlled_buffer_1_out[4]), .Q(To_Add_Sub[4]), .reset(in_2));  // open: Qn, preset, en
  D_Flip_Flop d_ff_4 (
    .clk(CLK), .D(controlled_buffer_1_out[3]), .Q(To_Add_Sub[3]), .reset(in_2));  // open: Qn, preset, en
  D_Flip_Flop d_ff_5 (
    .clk(CLK), .D(controlled_buffer_1_out[2]), .Q(To_Add_Sub[2]), .reset(in_2));  // open: Qn, preset, en
  D_Flip_Flop d_ff_6 (
    .clk(CLK), .D(controlled_buffer_1_out[1]), .Q(To_Add_Sub[1]), .reset(in_2));  // open: Qn, preset, en
  D_Flip_Flop D0 (.clk(CLK), .D(controlled_buffer_1_out[0]), .Q(To_Add_Sub[0]), .reset(in_2));  // open: Qn, preset, en
endmodule

module Output_Register (
  input  CLK,
  input  in_2,
  input  [7:0] From_Bus,
  input  nLo,
  output [7:0] To_Binary_Display
);

  wire not_1_out;
  wire [7:0] controlled_buffer_1_out;

  D_Flip_Flop D7 (
    .clk(CLK), .D(controlled_buffer_1_out[7]), .Q(To_Binary_Display[7]), .reset(in_2));  // open: Qn, preset, en
  D_Flip_Flop d_ff_1 (
    .clk(CLK), .D(controlled_buffer_1_out[6]), .Q(To_Binary_Display[6]), .reset(in_2));  // open: Qn, preset, en
  assign controlled_buffer_1_out = not_1_out ? From_Bus : 8'bz;  // Controlled_Buffer controlled_buffer_1
  not not_1 (not_1_out, nLo);
  D_Flip_Flop d_ff_2 (
    .clk(CLK), .D(controlled_buffer_1_out[5]), .Q(To_Binary_Display[5]), .reset(in_2));  // open: Qn, preset, en
  D_Flip_Flop d_ff_3 (
    .clk(CLK), .D(controlled_buffer_1_out[4]), .Q(To_Binary_Display[4]), .reset(in_2));  // open: Qn, preset, en
  D_Flip_Flop d_ff_4 (
    .clk(CLK), .D(controlled_buffer_1_out[3]), .Q(To_Binary_Display[3]), .reset(in_2));  // open: Qn, preset, en
  D_Flip_Flop d_ff_5 (
    .clk(CLK), .D(controlled_buffer_1_out[2]), .Q(To_Binary_Display[2]), .reset(in_2));  // open: Qn, preset, en
  D_Flip_Flop d_ff_6 (
    .clk(CLK), .D(controlled_buffer_1_out[1]), .Q(To_Binary_Display[1]), .reset(in_2));  // open: Qn, preset, en
  D_Flip_Flop D0 (
    .clk(CLK), .D(controlled_buffer_1_out[0]), .Q(To_Binary_Display[0]), .reset(in_2));  // open: Qn, preset, en
endmodule

// Instruction Decoder
module instruction_decoder (
  input  I7,
  input  I6,
  input  I5,
  input  I4,
  output LDA,
  output ADD,
  output SUB,
  output OUT,
  output HLT
);

  wire not_1_out, not_2_out, not_3_out, not_4_out;

  not not_1 (not_1_out, I7);
  not not_2 (not_2_out, I6);
  not not_3 (not_3_out, I4);
  not not_4 (not_4_out, I5);
  and and_1 (LDA, I7, not_2_out, I5, I4);
  and and_2 (ADD, not_1_out, I6, not_4_out, I4);
  and and_3 (SUB, not_1_out, I6, I5, I4);
  and and_4 (OUT, not_1_out, not_2_out, not_4_out, not_3_out);
  and and_5 (HLT, not_1_out, I6, not_4_out, not_3_out);
endmodule

// HA
module half_adder (
  input  A,
  input  B,
  output Sum,
  output Carry
);

  xor xor_1 (Sum, A, B);
  and and_1 (Carry, B, A);
endmodule

// Ring Counter
module ring_counter (
  input  CLK,
  output T1,
  output T2,
  output T3,
  output T4,
  output T5,
  output T6
);

  wire nor_1_out;

  nor nor_1 (nor_1_out, T1, T2, T3, T4, T5, T6);
  D_Flip_Flop D1 (.clk(CLK), .D(nor_1_out), .Q(T1));  // open: Qn, preset, en, reset
  D_Flip_Flop d_ff_1 (.clk(CLK), .D(T1), .Q(T2));  // open: Qn, preset, en, reset
  D_Flip_Flop d_ff_2 (.clk(CLK), .D(T2), .Q(T3));  // open: Qn, preset, en, reset
  D_Flip_Flop d_ff_3 (.clk(CLK), .D(T3), .Q(T4));  // open: Qn, preset, en, reset
  D_Flip_Flop d_ff_4 (.clk(CLK), .D(T4), .Q(T5));  // open: Qn, preset, en, reset
  D_Flip_Flop d_ff_5 (.clk(CLK), .D(T5), .Q(T6));  // open: Qn, preset, en, reset
endmodule

// FA
module full_adder (
  input  A,
  input  B,
  input  Cin,
  output Sum,
  output Cout
);

  wire and_1_out, and_2_out, xor_1_out;

  xor xor_1 (xor_1_out, A, B);
  and and_1 (and_1_out, A, B);
  xor xor_2 (Sum, xor_1_out, Cin);
  and and_2 (and_2_out, xor_1_out, Cin);
  or or_1 (Cout, and_2_out, and_1_out);
endmodule
